# Fritzing sketch Main (saved by Fritzing 0.9.3b)
circuit board: 4.1cm x 4.4cm
breadboards: 1

parts:
  Q3 = PNP-Transistor [package="TO92 [THT]"]
  Q4 = PNP-Transistor [package="TO92 [THT]"]
  SG2 = Buzzer 12mm [package=buzzer-12mm-ns]
  R5 = Resistor [tolerance=±5% resistance=220 package=THT]
  R6 = Resistor [tolerance=±5% resistance=220 package=THT]
  R7 = Resistor [tolerance=±5% resistance=220 package=THT]

nets:
  N1: Q3.B, R6.Pin_0
  N2: Q3.C, Q4.C, SG2.2, R5.Pin_1
  N3: Q4.B, R7.Pin_0
